// Logisim project task1.circ as structural Verilog: 1 circuit, main circuit main
module main (
  input  D0,
  input  D1,
  input  D2,
  input  D3,
  input  D4,
  input  D5,
  input  D6,
  input  D7,
  input  S2,
  input  S1,
  input  S0
);

  wire nand_1_out, nand_2_out, nand_3_out, nand_4_out, nand_5_out, nand_6_out, nand_7_out, nand_8_out,
       nand_9_out, nand_10_out, nand_11_out, nand_12_out, nand_13_out, nand_14_out, nand_15_out, nand_16_out,
       nor_1_out, not_1_out, not_2_out, not_3_out, not_4_out, not_5_out, not_6_out, not_7_out, not_8_out,
       not_9_out, not_10_out, not_11_out, not_12_out, not_13_out, not_14_out, not_15_out, not_16_out,
       not_17_out, not_18_out, not_19_out, not_20_out;

  // Probe on not_1_out
  not not_1 (not_1_out, nand_1_out);
  nand nand_1 (nand_1_out, not_5_out, not_6_out, not_8_out);
  // Probe on not_2_out
  not not_2 (not_2_out, nand_2_out);
  nand nand_2 (nand_2_out, not_5_out, not_6_out, S0);
  // Probe on not_3_out
  not not_3 (not_3_out, nand_3_out);
  nand nand_3 (nand_3_out, not_5_out, S1, not_8_out);
  // Probe on S2
  // Probe on not_4_out
  not not_4 (not_4_out, nand_4_out);
  nand nand_4 (nand_4_out, not_5_out, S1, S0);
  not not_5 (not_5_out, S2);
  // Probe on S1
  not not_6 (not_6_out, S1);
  // Probe on S0
  // Probe on not_7_out
  not not_7 (not_7_out, nand_5_out);
  nand nand_5 (nand_5_out, S2, not_6_out, not_8_out);
  not not_8 (not_8_out, S0);
  nand nand_6 (nand_6_out, D0, not_1_out);
  nand nand_7 (nand_7_out, D1, not_2_out);
  nand nand_8 (nand_8_out, D2, not_3_out);
  nand nand_9 (nand_9_out, D3, not_4_out);
  nand nand_10 (nand_10_out, D4, not_7_out);
  nand nand_11 (nand_11_out, D5, not_9_out);
  nand nand_12 (nand_12_out, D6, not_18_out);
  nand nand_13 (nand_13_out, D7, not_19_out);
  // Probe on not_9_out
  not not_9 (not_9_out, nand_14_out);
  nand nand_14 (nand_14_out, S2, not_6_out, S0);
  not not_10 (not_10_out, nand_6_out);
  not not_11 (not_11_out, nand_7_out);
  not not_12 (not_12_out, nand_8_out);
  not not_13 (not_13_out, nand_9_out);
  not not_14 (not_14_out, nand_10_out);
  not not_15 (not_15_out, nand_11_out);
  not not_16 (not_16_out, nand_12_out);
  not not_17 (not_17_out, nand_13_out);
  // Probe on not_18_out
  not not_18 (not_18_out, nand_15_out);
  nand nand_15 (nand_15_out, S2, S1, not_8_out);
  // Probe on not_19_out
  not not_19 (not_19_out, nand_16_out);
  nand nand_16 (nand_16_out, S2, S1, S0);
  nor nor_1 (nor_1_out, not_10_out, not_11_out, not_12_out, not_13_out, not_14_out, not_15_out, not_16_out, not_17_out);
  not not_20 (not_20_out, nor_1_out);
  // Probe on not_20_out

  // Notes on the sheet:
  //   8-входовой мультиплексор
  //   Земляная Дарья
  //   S2
  //   S1
  //   D0
  //   D1
  //   D2
  //   D3
  //   D4
  //   D5
  //   D6
  //   D7
  //   S0
  //   Y
endmodule
